// Logisim project ABCcircuit.circ as structural Verilog: 2 circuits, main circuit main
module main (
  input  X,
  input  Y,
  input  Z
);

  wire alpha_7segment_decoder_1_c0, alpha_7segment_decoder_1_c1, alpha_7segment_decoder_1_c2,
       alpha_7segment_decoder_1_c3, alpha_7segment_decoder_1_c4, alpha_7segment_decoder_1_c5,
       alpha_7segment_decoder_1_c6;

  Alpha_7Segment_Decoder alpha_7segment_decoder_1 (
    .X(X), .Y(Y), .Z(Z), .C0(alpha_7segment_decoder_1_c0), .C1(alpha_7segment_decoder_1_c1),
    .C2(alpha_7segment_decoder_1_c2), .C3(alpha_7segment_decoder_1_c3), .C4(alpha_7segment_decoder_1_c4),
    .C5(alpha_7segment_decoder_1_c5), .C6(alpha_7segment_decoder_1_c6));
  _7_Segment_Display u_7_segment_display_1 (
    .g(alpha_7segment_decoder_1_c6), .f(alpha_7segment_decoder_1_c5), .a(alpha_7segment_decoder_1_c0),
    .b(alpha_7segment_decoder_1_c1), .e(alpha_7segment_decoder_1_c4), .d(alpha_7segment_decoder_1_c3),
    .c(alpha_7segment_decoder_1_c2));  // open: dp
endmodule

module Alpha_7Segment_Decoder (
  input  X,
  input  Y,
  input  Z,
  output C0,
  output C1,
  output C2,
  output C3,
  output C4,
  output C5,
  output C6
);

  wire not_1_out, not_2_out, not_3_out, X_prime_Y_out, X_prime_Y_prime___X_prime_Z_prime_out,
       X_prime_Y_prime_out, X_prime_Z_prime_out, XY_prime_out, Y_prime_Z_out, Y_prime_Z_prime_out,
       YZ_prime_out;

  not not_1 (not_1_out, X);
  not not_2 (not_2_out, Z);
  not not_3 (not_3_out, Y);
  and X_prime_Y_prime (X_prime_Y_prime_out, not_1_out, not_3_out);
  and X_prime_Z_prime (X_prime_Z_prime_out, not_1_out, not_2_out);
  and Y_prime_Z_prime (Y_prime_Z_prime_out, not_3_out, not_2_out);
  and X_prime_Y (X_prime_Y_out, not_1_out, Y);
  and XY_prime (XY_prime_out, X, not_3_out);
  and YZ_prime (YZ_prime_out, Y, not_2_out);
  and Y_prime_Z (Y_prime_Z_out, not_3_out, Z);
  or X_prime_Y_prime___X_prime_Z_prime (X_prime_Y_prime___X_prime_Z_prime_out, X_prime_Y_prime_out, X_prime_Z_prime_out);
  or u_C3 (C3, X_prime_Y_out, XY_prime_out);
  or C1__C2 (C1, X_prime_Y_prime___X_prime_Z_prime_out, Y_prime_Z_prime_out);
  or or_1 (C6, YZ_prime_out, Y_prime_Z_out);

  assign C0 = 1'b1;
  assign C2 = C1;
  assign C4 = 1'b1;
  assign C5 = 1'b1;
endmodule
