// Logisim project Lab05_2-bitComparator.circ as structural Verilog: 2 circuits, main circuit main
module main (
  input  A1,
  input  A0,
  input  B1,
  input  B0
);

  wire alpha_display_1_c0, alpha_display_1_c1, alpha_display_1_c2, alpha_display_1_c3, alpha_display_1_c4,
       alpha_display_1_c5, alpha_display_1_c6;

  Alpha_Display alpha_display_1 (
    .A1(A1), .A0(A0), .B1(B1), .B0(B0), .C0(alpha_display_1_c0), .C1(alpha_display_1_c1),
    .C2(alpha_display_1_c2), .C3(alpha_display_1_c3), .C4(alpha_display_1_c4), .C5(alpha_display_1_c5),
    .C6(alpha_display_1_c6));
  _7_Segment_Display u_7_segment_display_1 (
    .g(alpha_display_1_c6), .f(alpha_display_1_c5), .a(alpha_display_1_c0), .b(alpha_display_1_c1),
    .e(alpha_display_1_c4), .d(alpha_display_1_c3), .c(alpha_display_1_c2));  // open: dp
endmodule

module Alpha_Display (
  input  A1,
  input  A0,
  input  B1,
  input  B0,
  output C0,
  output C1,
  output C2,
  output C3,
  output C4,
  output C5,
  output C6
);

  wire A_prime_B_prime_out, A_prime_C_out, A_prime_D_out, AC_prime_out, B_prime_C_out, B_prime_D_out,
       BD_prime_out, CD_out, not_1_out, not_2_out, not_3_out, not_4_out, or_1_out, or_2_out, or_3_out,
       or_4_out, or_5_out;

  not not_1 (not_1_out, A1);
  not not_2 (not_2_out, A0);
  not not_3 (not_3_out, B1);
  not not_4 (not_4_out, B0);
  and B_prime_D (B_prime_D_out, not_2_out, B0);
  and BD_prime (BD_prime_out, A0, not_4_out);
  and AC_prime (AC_prime_out, A1, not_3_out);
  and A_prime_D (A_prime_D_out, not_1_out, B0);
  and A_prime_B_prime (A_prime_B_prime_out, not_1_out, not_2_out);
  and B_prime_C (B_prime_C_out, not_2_out, B1);
  and A_prime_C (A_prime_C_out, not_1_out, B1);
  and CD (CD_out, B1, B0);
  or or_1 (or_1_out, B_prime_D_out, BD_prime_out);
  or or_2 (or_2_out, AC_prime_out, A_prime_C_out);
  or or_3 (or_3_out, A_prime_C_out, A_prime_D_out);
  or or_4 (or_4_out, CD_out, A_prime_B_prime_out);
  or C1_C2 (C1, or_1_out, or_2_out);
  or or_5 (or_5_out, or_3_out, or_4_out);
  or or_6 (C3, or_5_out, B_prime_C_out);

  assign C0 = 1'b1;
  assign C2 = C1;
  assign C4 = 1'b1;
  assign C5 = 1'b1;
  assign C6 = 1'b1;
endmodule
