// Logisim project Q2_B_67070041.circ as structural Verilog: 3 circuits, main circuit main
module main (
  input  A,
  input  B,
  input  C,
  input  D
);

  wire chardecoderv2_1_c0, chardecoderv2_1_c1, chardecoderv2_1_c2, chardecoderv2_1_c3, chardecoderv2_1_c4,
       chardecoderv2_1_c5, chardecoderv2_1_c6, graderv2_1_x, graderv2_1_y, graderv2_1_z;

  graderV2 graderv2_1 (.A(A), .B(B), .C(C), .D(D), .X(graderv2_1_x), .Y(graderv2_1_y), .Z(graderv2_1_z));
  charDecoderV2 chardecoderv2_1 (
    .X(graderv2_1_x), .Y(graderv2_1_y), .Z(graderv2_1_z), .C0(chardecoderv2_1_c0), .C1(chardecoderv2_1_c1),
    .C2(chardecoderv2_1_c2), .C3(chardecoderv2_1_c3), .C4(chardecoderv2_1_c4), .C5(chardecoderv2_1_c5),
    .C6(chardecoderv2_1_c6));
  _7_Segment_Display u_7_segment_display_1 (
    .g(chardecoderv2_1_c6), .f(chardecoderv2_1_c5), .a(chardecoderv2_1_c0), .b(chardecoderv2_1_c1),
    .e(chardecoderv2_1_c4), .d(chardecoderv2_1_c3), .c(chardecoderv2_1_c2));  // open: dp

  // Notes on the sheet:
  //   graderV2
  //   charDecoderV2
  //   Tanapat Tiptaingtae
  //   67070041
endmodule

module charDecoderV2 (
  input  X,
  input  Y,
  input  Z,
  output C0,
  output C1,
  output C2,
  output C3,
  output C4,
  output C5,
  output C6
);

  wire not_2_out, not_3_out;

  not not_1 (C3, X);
  not not_2 (not_2_out, Y);
  not not_3 (not_3_out, Z);
  or X_Y (C5, X, Y);
  or X_Z (C6, X, Z);
  or X_Z_prime (C0, X, not_3_out);
  and Y_prime_Z (C1, not_2_out, Z);

  assign C2 = Z;
  assign C4 = 1'b1;
endmodule

module graderV2 (
  input  A,
  input  B,
  input  C,
  input  D,
  output X,
  output Y,
  output Z
);

  wire A_prime_B_prime_out, AB_prime_out, ABC_out, ABD_out, AC_prime_D_prime_out, ACD_out, not_1_out,
       not_2_out, not_3_out, not_4_out;

  not not_1 (not_1_out, A);
  not not_2 (not_2_out, B);
  not not_3 (not_3_out, C);
  not not_4 (not_4_out, D);
  and A_prime_B_prime (A_prime_B_prime_out, not_1_out, not_2_out);
  and ABC (ABC_out, A, B, C);
  and ABD (ABD_out, A, B, D);
  and AB_prime (AB_prime_out, A, not_2_out);
  and AC_prime_D_prime (AC_prime_D_prime_out, A, not_3_out, not_4_out);
  and ACD (ACD_out, A, C, D);
  or u_X (X, A_prime_B_prime_out, ABC_out, ABD_out);
  or u_Y (Y, AB_prime_out, AC_prime_D_prime_out);
  or u_Z (Z, ACD_out, B);
endmodule
