// Logisim project megabitSegment.circ as structural Verilog: 3 circuits, main circuit main
module main (
  input  W,
  input  X,
  input  Y,
  input  Z
);

  wire bcd_7seg_decoder_1_c0, bcd_7seg_decoder_1_c1, bcd_7seg_decoder_1_c2, bcd_7seg_decoder_1_c3,
       bcd_7seg_decoder_1_c4, bcd_7seg_decoder_1_c5, bcd_7seg_decoder_1_c6, bcd_7seg_decoder_2_c0,
       bcd_7seg_decoder_2_c1, bcd_7seg_decoder_2_c2, bcd_7seg_decoder_2_c3, bcd_7seg_decoder_2_c4,
       bcd_7seg_decoder_2_c5, bcd_7seg_decoder_2_c6, double_1_g0, double_1_g1, double_1_g2, double_1_g3,
       double_1_h0, double_1_h1, double_1_h2, double_1_h3;

  double double_1 (
    .W(W), .X(X), .Y(Y), .Z(Z), .G3(double_1_g3), .G2(double_1_g2), .G1(double_1_g1), .G0(double_1_g0),
    .H3(double_1_h3), .H2(double_1_h2), .H1(double_1_h1), .H0(double_1_h0));
  BCD_7seg_Decoder bcd_7seg_decoder_1 (
    .A(double_1_g3), .B(double_1_g2), .C(double_1_g1), .D(double_1_g0), .C0(bcd_7seg_decoder_1_c0),
    .C1(bcd_7seg_decoder_1_c1), .C2(bcd_7seg_decoder_1_c2), .C3(bcd_7seg_decoder_1_c3),
    .C4(bcd_7seg_decoder_1_c4), .C5(bcd_7seg_decoder_1_c5), .C6(bcd_7seg_decoder_1_c6));
  BCD_7seg_Decoder bcd_7seg_decoder_2 (
    .A(double_1_h3), .B(double_1_h2), .C(double_1_h1), .D(double_1_h0), .C0(bcd_7seg_decoder_2_c0),
    .C1(bcd_7seg_decoder_2_c1), .C2(bcd_7seg_decoder_2_c2), .C3(bcd_7seg_decoder_2_c3),
    .C4(bcd_7seg_decoder_2_c4), .C5(bcd_7seg_decoder_2_c5), .C6(bcd_7seg_decoder_2_c6));
  _7_Segment_Display u_7_segment_display_1 (
    .g(bcd_7seg_decoder_1_c6), .f(bcd_7seg_decoder_1_c5), .a(bcd_7seg_decoder_1_c0),
    .b(bcd_7seg_decoder_1_c1), .e(bcd_7seg_decoder_1_c4), .d(bcd_7seg_decoder_1_c3), .c(bcd_7seg_decoder_1_c2));  // open: dp
  _7_Segment_Display u_7_segment_display_2 (
    .g(bcd_7seg_decoder_2_c6), .f(bcd_7seg_decoder_2_c5), .a(bcd_7seg_decoder_2_c0),
    .b(bcd_7seg_decoder_2_c1), .e(bcd_7seg_decoder_2_c4), .d(bcd_7seg_decoder_2_c3), .c(bcd_7seg_decoder_2_c2));  // open: dp
endmodule

module BCD_7seg_Decoder (
  input  A,
  input  B,
  input  C,
  input  D,
  output C0,
  output C1,
  output C2,
  output C3,
  output C4,
  output C5,
  output C6
);

  wire A_prime_B_prime_out, B_prime_C_out, B_prime_D_prime_out, BC_prime_D_out, BC_prime_out, BCD_prime_out,
       BD_out, C_prime_D_prime_out, CD_out, CD_prime_out, not_1_out, not_2_out, not_3_out, not_4_out;

  not not_1 (not_1_out, B);
  not not_2 (not_2_out, A);
  not not_3 (not_3_out, C);
  not not_4 (not_4_out, D);
  and BD (BD_out, B, D);
  // AND_Gate B_prime_D has open pins: in0=not_1_out, in1=D, out=open
  // AND_Gate AC has open pins: in0=A, in1=C, out=open
  and A_prime_B_prime (A_prime_B_prime_out, not_2_out, not_1_out);
  and CD (CD_out, C, D);
  and C_prime_D_prime (C_prime_D_prime_out, not_3_out, not_4_out);
  and B_prime_C (B_prime_C_out, not_1_out, C);
  and B_prime_D_prime (B_prime_D_prime_out, not_1_out, not_4_out);
  and CD_prime (CD_prime_out, C, not_4_out);
  and BC_prime (BC_prime_out, B, not_3_out);
  and BC_prime_D (BC_prime_D_out, BD_out, not_3_out);
  and BCD_prime (BCD_prime_out, B, CD_prime_out);
  or u_C0 (C0, BD_out, B_prime_D_prime_out, A, C);
  or u_C1 (C1, A, A_prime_B_prime_out, CD_out, C_prime_D_prime_out);
  or u_C3 (C3, BC_prime_D_out, B_prime_C_out, B_prime_D_prime_out, CD_prime_out);
  or u_C2 (C2, A, B, not_3_out, D);
  or u_C4 (C4, CD_prime_out, B_prime_D_prime_out);
  or u_C5 (C5, A, C_prime_D_prime_out, BCD_prime_out, BC_prime_out);
  or u_C6 (C6, B_prime_C_out, CD_prime_out, A, BC_prime_out);
endmodule

module double (
  input  W,
  input  X,
  input  Y,
  input  Z,
  output G3,
  output G2,
  output G1,
  output G0,
  output H3,
  output H2,
  output H1,
  output H0
);

  wire not_1_out, not_2_out, not_3_out, not_4_out, W_prime_X_prime_Y_out, W_prime_X_prime_Z_out,
       W_prime_XY_out, W_prime_XY_prime_Z_prime_out, W_prime_XZ_out, W_prime_YZ_out, WX_out,
       WX_prime_Y_prime_out, WX_prime_Y_prime_Z_out, WX_prime_Y_prime_Z_prime_out, WX_prime_YZ_out,
       WXY_prime_out, WXY_prime_Z_out, WXYZ_prime_out, WY_out, XYZ_out;

  not not_1 (not_1_out, X);
  not not_2 (not_2_out, W);
  not not_3 (not_3_out, Z);
  not not_4 (not_4_out, Y);
  and WX (WX_out, W, X);
  and WY (WY_out, W, Y);
  and W_prime_XZ (W_prime_XZ_out, not_2_out, X, Z);
  and W_prime_XY (W_prime_XY_out, not_2_out, X, Y);
  and XYZ (XYZ_out, X, Y, Z);
  and W_prime_X_prime_Z (W_prime_X_prime_Z_out, not_2_out, not_1_out, Z);
  and WX_prime_Y_prime_Z_prime (WX_prime_Y_prime_Z_prime_out, W, not_1_out, not_4_out, not_3_out);
  and W_prime_YZ (W_prime_YZ_out, not_2_out, Y, Z);
  and WXY_prime_Z (WXY_prime_Z_out, W, X, not_4_out, Z);
  and W_prime_XY_prime_Z_prime (W_prime_XY_prime_Z_prime_out, not_2_out, X, not_4_out, not_3_out);
  and WX_prime_Y_prime_Z (WX_prime_Y_prime_Z_out, W, not_1_out, not_4_out, Z);
  and WXYZ_prime (WXYZ_prime_out, W, X, Y, not_3_out);
  and WX_prime_Y_prime (WX_prime_Y_prime_out, W, not_1_out, not_4_out);
  // AND_Gate W_prime_XYZ_prime has open pins: in0=not_2_out, in1=X, in2=Y, in3=not_3_out, out=open
  and W_prime_X_prime_Y (W_prime_X_prime_Y_out, not_2_out, not_1_out, Y);
  and WXY_prime (WXY_prime_out, not_4_out, WX_out);
  // AND_Gate WY_prime_Z_prime has open pins: in0=W, in1=not_4_out, in2=not_3_out, out=open
  and WX_prime_YZ (WX_prime_YZ_out, W, not_1_out, Y, Z);
  // AND_Gate WXYZ has open pins: in2=WX_out, in3=Y, in4=Z, out=open
  // AND_Gate WXY_prime_Z_2 has open pins: in0=WX_out, in1=not_4_out, out=open
  // AND_Gate WXY_prime_2 has open pins: in0=WX_out, in1=not_4_out, out=open
  or u_G0 (G0, W_prime_XY_out, W_prime_XZ_out, WX_prime_Y_prime_out, XYZ_out);
  or u_G1 (G1, WX_out, WY_out);
  or u_H1 (H1, W_prime_X_prime_Z_out, WXY_prime_out, WX_prime_YZ_out);
  or u_H2 (H2, W_prime_YZ_out, W_prime_X_prime_Y_out, WX_prime_Y_prime_Z_prime_out, WXY_prime_Z_out);
  or u_H3 (H3, W_prime_XY_prime_Z_prime_out, WX_prime_Y_prime_Z_out, WXYZ_prime_out);

  assign G2 = 1'b0;
  assign G3 = 1'b0;
  assign H0 = 1'b0;
endmodule
