// Logisim project sevenSegmentTest.circ as structural Verilog: 2 circuits, main circuit main
module main (
  input  A,
  input  B,
  input  C,
  input  D
);

  wire bcd_7seg_decoder_1_c0, bcd_7seg_decoder_1_c1, bcd_7seg_decoder_1_c2, bcd_7seg_decoder_1_c3,
       bcd_7seg_decoder_1_c4, bcd_7seg_decoder_1_c5, bcd_7seg_decoder_1_c6;

  BCD_7Seg_Decoder bcd_7seg_decoder_1 (
    .A(A), .B(B), .C(C), .D(D), .C0(bcd_7seg_decoder_1_c0), .C1(bcd_7seg_decoder_1_c1),
    .C2(bcd_7seg_decoder_1_c2), .C3(bcd_7seg_decoder_1_c3), .C4(bcd_7seg_decoder_1_c4),
    .C5(bcd_7seg_decoder_1_c5), .C6(bcd_7seg_decoder_1_c6));
  _7_Segment_Display u_7_segment_display_1 (
    .g(bcd_7seg_decoder_1_c6), .f(bcd_7seg_decoder_1_c5), .a(bcd_7seg_decoder_1_c0),
    .b(bcd_7seg_decoder_1_c1), .e(bcd_7seg_decoder_1_c4), .d(bcd_7seg_decoder_1_c3), .c(bcd_7seg_decoder_1_c2));  // open: dp
endmodule

module BCD_7Seg_Decoder (
  input  A,
  input  B,
  input  C,
  input  D,
  output C0,
  output C1,
  output C2,
  output C3,
  output C4,
  output C5,
  output C6
);

  wire A_prime_B_prime_out, A_prime_C_out, AD_out, B_prime_D_prime_out, BC_prime_D_out, BC_prime_out, BD_out,
       BD_prime_out, C_prime_D_prime_out, CD_prime_out, not_1_out, not_2_out, not_3_out, not_4_out;

  not not_1 (not_1_out, A);
  not not_2 (not_2_out, B);
  not not_3 (not_3_out, C);
  not not_4 (not_4_out, D);
  and BD (BD_out, B, D);
  and B_prime_D_prime (B_prime_D_prime_out, not_2_out, not_4_out);
  and A_prime_C (A_prime_C_out, not_1_out, C);
  and A_prime_B_prime (A_prime_B_prime_out, not_1_out, not_2_out);
  and BC_prime_D (BC_prime_D_out, B, not_3_out, D);
  and BD_prime (BD_prime_out, B, not_4_out);
  and CD_prime (CD_prime_out, C, not_4_out);
  and AD (AD_out, A, D);
  and BC_prime (BC_prime_out, B, not_3_out);
  // AND_Gate B_prime_C has open pins: in0=not_2_out, in1=C, out=open
  and C_prime_D_prime (C_prime_D_prime_out, not_3_out, not_4_out);
  or u_C6 (C6, A, BC_prime_out, CD_prime_out, BC_prime_out);
  or u_C0 (C0, BD_out, A, C, B_prime_D_prime_out);
  or u_C1 (C1, A_prime_C_out, A, A_prime_B_prime_out, AD_out);
  or u_C2 (C2, not_3_out, B, D);
  or u_C3 (C3, B_prime_D_prime_out, A_prime_C_out, CD_prime_out, BC_prime_D_out);
  or u_C4 (C4, B_prime_D_prime_out, C_prime_D_prime_out);
  or u_C5 (C5, C_prime_D_prime_out, BC_prime_out, not_3_out, BD_prime_out);
endmodule
